// Logisim project ALU_control.circ as structural Verilog: 1 circuit, main circuit main
module main (
  input  [1:0] Function,
  input  zero,
  input  [2:0] ALUop,
  output [1:0] ALUctr
);

  wire or_1_out;
  wire [0:0] and_1_out;

  and and_1 (and_1_out[0], ALUop[0], ALUop[1]);
  or or_1 (or_1_out, ALUop[0], ALUop[1], ALUop[2]);
  Multiplexer #(.width(2)) multiplexer_1 (
    .in0(Function), .in1({zero, and_1_out[0]}), .out(ALUctr), .sel(or_1_out));  // open: en
endmodule
