// Logisim project Control_Unit.circ as structural Verilog: 1 circuit, main circuit main
module main (
  input  [3:0] Op_code,
  output [2:0] ALUop,
  output Jcont,
  output RegWrite,
  output RegDst,
  output ALUsrc,
  output MemWrite,
  output Branch,
  output Extop,
  output MemRead,
  output MemToReg
);

  wire [3:3] undriven;

  and R_type (RegDst, ~ALUop[0], ~ALUop[1], ~ALUop[2], ~undriven[3]);  // AND_Gate
  and Lw (MemRead, ~ALUop[0], ~ALUop[1], ~ALUop[2], undriven[3]);  // AND_Gate
  and Sw (MemWrite, ~ALUop[0], ~ALUop[1], ALUop[2], ~undriven[3]);  // AND_Gate
  and Beq (Branch, ~ALUop[0], ~ALUop[1], ALUop[2], undriven[3]);  // AND_Gate
  and J (Jcont, ~ALUop[0], ALUop[1], ~ALUop[2], ~undriven[3]);  // AND_Gate
  or or_1 (RegWrite, MemRead, RegDst);
  or or_2 (ALUsrc, MemWrite, MemRead);
  or or_3 (Extop, Branch, MemWrite, MemRead);

  assign MemToReg = MemRead;
endmodule
