// Logisim project alu.circ as structural Verilog: 1 circuit, main circuit main
module main (
  input  [17:0] A,
  input  [17:0] B,
  input  [1:0] select,
  output [17:0] Y,
  output out_5
);

  wire [17:0] adder_1_out, AND_out, OR_out, subtractor_1_out;

  Adder #(.width(18)) adder_1 (.a(A), .b(B), .out(adder_1_out));  // open: cin, cout
  Subtractor #(.width(18)) subtractor_1 (.a(A), .b(B), .out(subtractor_1_out));  // open: bin, bout
  assign OR_out = A | B;  // OR_Gate OR, 18 bits wide
  assign AND_out = A & B;  // AND_Gate AND, 18 bits wide
  Multiplexer #(.select(2), .width(18)) multiplexer_1 (
    .in0(adder_1_out), .in1(subtractor_1_out), .in2(OR_out), .in3(AND_out), .out(Y), .sel(select));  // open: en
  and zero_check (out_5, Y[0], Y[1], Y[2], Y[3], Y[4], Y[5], Y[6], Y[7], Y[8], Y[9], Y[10], Y[11], Y[12], Y[13], Y[14], Y[15], Y[16], Y[17]);
endmodule
